# Fritzing sketch Battery Status (saved by Fritzing 0.9.4)
breadboards: 1

parts:
  Part1 = FTDI Basic Programmer
  C1 = Electrolytic Capacitor [capacitance=1µF package="100 mil [THT, electrolytic]"]
  R1 = Resistor [tolerance=±5% resistance=10k package=THT]
  R2 = Resistor [tolerance=±5% resistance=10k package=THT]
  S1 = Pushbutton [package="[THT]"]
  S2 = Pushbutton [package="[THT]"]
  C2 = Capacitor [package=cap-pth-small2]
  R3 = Resistor [tolerance=±5% resistance=10k package=THT]
  U2 = ESP8266 WiFi Module [part_number=ESP8266]
  U3 = ESP8266 WiFi Module [part_number=ESP8266]  # not connected
  BAT1 = Battery Holders [package=battery-aa]
  R4 = Resistor [tolerance=±5% resistance=220 package=THT]
  R5 = Resistor [tolerance=±5% resistance=220 package=THT]
  U4 = Voltage Regulator - 5V [package="TO220 [THT]"]
  C3 = Electrolytic Capacitor [capacitance=1µF package="100 mil [THT, electrolytic]"]

nets:
  N1: Part1.RXI, U2.TXD
  N2: Part1.TXO, U2.RXD
  N3: Part1.POWER, C1.+, R1.Pin_1, R2.Pin_1, C2.2, R3.Pin_0, U2.VCC, U4.output_voltage, C3.+
  GND: Part1.GND, C1.-, S1.Pin_3, S1.Pin_4, S2.Pin_3, S2.Pin_4, C2.1, U2.GND, U2.GPIO_15, BAT1.-, R4.Pin_0, U4.GND, C3.-
  N4: R1.Pin_0, S1.Pin_1, S1.Pin_2, U2.GPIO_0
  N5: R2.Pin_0, S2.Pin_1, S2.Pin_2, U2.REST
  N6: R3.Pin_1, U2.CH_PD
  N7: U2.ADC_0, R4.Pin_1, R5.Pin_0
  N8: BAT1.+, R5.Pin_1, U4.input_voltage

notes:
  PROGRAM
  RESET
  https://www.studiopieters.nl
  RST
  ADC
  CH_PD
  GPIO16
  GPIO14
  GPIO12
  GPIO13
  VCC
  TXD
  GPIO4
  GPIO0
  GPIO5
  GPIO15
  GPIO2
  GND
  CS0
  MOSI
  GPIO10
  GPIO9
  SCLK
  MISO

custom parts:
  FTDI Basic Programmer: Description: This is the newest revision of our FTDI Basic. We now use a SMD 6-pin header on the bottom, which makes it smaller and more compact. Functionality has remained the same. This is a basic breakout board for the FTDI FT232RL USB to serial IC. The pinout of this board matches the FTDI cable to work with official Arduino and cloned 3.3V Arduino boards. It can also be used for general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
  ESP8266 WiFi Module: Generic WiFi Module based on the ESP8266 with onboard PCB antenna and UART communications
  Battery Holders: Battery Holders Various common sizes : AA, AAA, 20mm coin cell and 12mm coin cell.
